# Fritzing sketch ESP32 Soccer Bot PCB (saved by Fritzing 0.9.4)
breadboards: 1

parts:
  U1 = ESP32S-HiLetgo [part_number=ESP32S-HiLetgo]
  VCC1 = Battery
  J1 = female pin header, 17 pins [form="♀ (female)"]
  J2 = female pin header, 17 pins [form="♀ (female)"]
  J3 = female pin header, 5 pins [form="♀ (female)"]
  J4 = female pin header, 5 pins [form="♀ (female)"]
  J5 = female pin header, 5 pins [form="♀ (female)"]

nets:
  N1: U1.3.3, J2.pin17, J4.pin1, J4.pin2, J4.pin3, J4.pin4, J4.pin5
  N2: U1.EN, J2.pin16
  N3: U1.GPIO36, J2.pin15
  N4: U1.GPIO39, J2.pin14
  N5: U1.GPIO34, J2.pin13
  N6: U1.GPIO35, J2.pin12
  N7: U1.GPIO32, J2.pin11
  N8: U1.GPIO33, J2.pin10
  N9: U1.GPIO25, J2.pin9
  N10: U1.GPIO26, J2.pin8
  N11: U1.GPIO27, J2.pin7
  N12: U1.GPIO14, J2.pin6
  N13: U1.GPIO12, J2.pin5
  N14: U1.GPIO13, J2.pin4
  N15: U1.GPIO9, J2.pin3
  N16: U1.GPIO10, J2.pin2
  N17: U1.GPIO11, J2.pin1
  N18: U1.VIN, VCC1.+, J3.pin1, J3.pin2, J3.pin3, J3.pin4, J3.pin5
  N19: U1.GPIO6, J1.pin17
  N20: U1.GPIO7, J1.pin16
  N21: U1.GPIO8, J1.pin15
  N22: U1.GPIO15, J1.pin14
  N23: U1.GPIO2, J1.pin13
  N24: U1.GPIO0, J1.pin12
  N25: U1.GPIO4, J1.pin11
  N26: U1.GPIO16, J1.pin10
  N27: U1.GPIO17, J1.pin9
  N28: U1.GPIO5, J1.pin8
  N29: U1.GPIO18, J1.pin7
  N30: U1.GPIO19, J1.pin6
  N31: U1.GPIO21, J1.pin5
  N32: U1.GPIO3, J1.pin4
  N33: U1.GPIO1, J1.pin3
  N34: U1.GPIO22, J1.pin2
  N35: U1.GPIO23, J1.pin1
  N36: U1.GND, VCC1.-, J5.pin1, J5.pin2, J5.pin3, J5.pin4, J5.pin5

custom parts:
  ESP32S-HiLetgo: HiLetgo ESP-WROOM-32 ESP32 ESP-32S Development Board 2.4GHz Dual-Mode WiFi + Bluetooth Dual Cores Microcontroller The ESP32 integrated with Antenna switches, RF Balun, power amplifiers, low-noise amplifiers, filters, and management modules, and the entire solution occupies the least area of PCB. 2.4 GHz Wi-Fi plus Bluetooth dual-mode chip, with TSMC Ultra-low power consumption 40nm technology,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
