# Fritzing sketch ESP32 Soccer Bot PCB (saved by Fritzing 0.9.4)
circuit board: 5.5651cm x 5.35986cm
breadboards: 1

parts:
  D23 = female pin header, 14 pins [form="♀ (female)"]
  EN-Vin = female pin header, 13 pins [form="♀ (female)"]
  +5V- = Battery
  3_3V = female pin header, 5 pins [form="♀ (female)"]
  5V = female pin header, 5 pins [form="♀ (female)"]
  GND = female pin header, 5 pins [form="♀ (female)"]
  OFF/ON = Toggle Switch [package=THT]
  USB_SIDE = LuaNode32 / ESP32 [part_number=ESP32S-PIN30]

nets:
  N1: D23.pin1, USB_SIDE.D23
  N2: D23.pin2, USB_SIDE.D22
  N3: D23.pin3, USB_SIDE.TX0
  N4: D23.pin4, USB_SIDE.RX0
  N5: D23.pin5, USB_SIDE.D21
  N6: D23.pin6, USB_SIDE.D19
  N7: D23.pin7, USB_SIDE.D18
  N8: D23.pin8, USB_SIDE.D5
  N9: D23.pin9, USB_SIDE.TX2
  N10: D23.pin10, USB_SIDE.RX2
  N11: D23.pin11, USB_SIDE.D4
  N12: D23.pin12, USB_SIDE.D2
  N13: D23.pin13, USB_SIDE.D15
  N14: D23.pin14, +5V-.-, GND.pin1, GND.pin2, GND.pin3, GND.pin4, GND.pin5, USB_SIDE.GND
  N15: EN-Vin.pin1, USB_SIDE.D13
  N16: EN-Vin.pin2, USB_SIDE.D12
  N17: EN-Vin.pin3, USB_SIDE.D14
  N18: EN-Vin.pin4, USB_SIDE.D27
  N19: EN-Vin.pin5, USB_SIDE.D26
  N20: EN-Vin.pin6, USB_SIDE.D25
  N21: EN-Vin.pin7, USB_SIDE.D33
  N22: EN-Vin.pin8, USB_SIDE.D32
  N23: EN-Vin.pin9, USB_SIDE.D35
  N24: EN-Vin.pin10, USB_SIDE.D34
  N25: EN-Vin.pin11, USB_SIDE.VN
  N26: EN-Vin.pin12, USB_SIDE.VP
  N27: EN-Vin.pin13, USB_SIDE.EN
  N28: +5V-.+, OFF/ON.L2
  N29: 3_3V.pin1, 3_3V.pin2, 3_3V.pin3, 3_3V.pin4, 3_3V.pin5, USB_SIDE.3V3
  N30: 5V.pin1, 5V.pin2, 5V.pin3, 5V.pin4, 5V.pin5, OFF/ON.COM, USB_SIDE.Vin

notes:
  AYM

custom parts:
  LuaNode32 / ESP32: New Image for LuaNode32 DOIT ESP32 DEVKIT V1. Base parts from LuaNode32 / ESP32 ESP32 based LuaNode32 by G.Noorlander DOIT Esp32 DevKit v1 (30 pins long, 11 pins width) by Werner Rothschopf (modified by vanepp Dec 2018)
